// Logisim project main-circuit.circ as structural Verilog
module D_Latch (
  input  D,
  input  Enable,
  output Q,
  output Q_prime
);

  wire nand_1_out, nand_2_out, not_1_out;

  nand nand_1 (nand_1_out, D, Enable);
  nand nand_2 (nand_2_out, Enable, not_1_out);
  not not_1 (not_1_out, D);
  nand nand_3 (Q, nand_1_out, Q_prime);
  nand nand_4 (Q_prime, Q, nand_2_out);
endmodule

module D_FF (
  input  D,
  input  Clk,
  output Q
);

  wire d_latch_1_q, not_1_out;

  D_Latch d_latch_1 (.D(D), .Enable(Clk), .Q(d_latch_1_q));  // open: Q_prime
  D_Latch d_latch_2 (.D(d_latch_1_q), .Enable(not_1_out), .Q(Q));  // open: Q_prime
  not not_1 (not_1_out, Clk);
endmodule

module _8_bit_register (
  input  Clk,
  input  [7:0] Output,
  output [7:0] out_3
);

  D_FF d_ff_1 (.D(Output[7]), .Clk(Clk), .Q(out_3[7]));
  D_FF d_ff_2 (.D(Output[6]), .Clk(Clk), .Q(out_3[6]));
  D_FF d_ff_3 (.D(Output[5]), .Clk(Clk), .Q(out_3[5]));
  D_FF d_ff_4 (.D(Output[4]), .Clk(Clk), .Q(out_3[4]));
  D_FF d_ff_5 (.D(Output[3]), .Clk(Clk), .Q(out_3[3]));
  D_FF d_ff_6 (.D(Output[2]), .Clk(Clk), .Q(out_3[2]));
  D_FF d_ff_7 (.D(Output[1]), .Clk(Clk), .Q(out_3[1]));
  D_FF d_ff_8 (.D(Output[0]), .Clk(Clk), .Q(out_3[0]));

  // Notes on the sheet:
  //   Little Endian
endmodule
